// Logisim project podium.circ as structural Verilog: 1 circuit, main circuit main
module main (
  input  in_1,
  input  in_2,
  input  in_3,
  input  in_4,
  input  in_5,
  output out_6,
  output out_7,
  output out_8,
  output out_9,
  output out_10,
  output out_11
);

  wire and_2_out, not_1_out, not_2_out, not_3_out, not_4_out;

  buf and_1 (in_3, in_1);  // AND_Gate
  and and_2 (and_2_out, in_2, in_3);
  and and_3 (out_9, in_4, in_5);
  not not_1 (not_1_out, in_5);
  not not_2 (not_2_out, in_4);
  and and_4 (out_6, in_3, and_2_out);
  not not_3 (not_3_out, and_2_out);
  not not_4 (not_4_out, in_3);
  and and_5 (out_10, in_4, not_1_out);
  and and_6 (out_11, not_2_out, in_5);
  and and_7 (out_7, in_3, not_3_out);
  and and_8 (out_8, not_4_out, and_2_out);
endmodule
